# Fritzing sketch cableado (saved by Fritzing 0.9.9b)

parts:
  Componente1 = Arduino Nano (Rev3.0) (ICSP)
  Componente2 = Matrix LED de 8x8 basada en MAX7219
  Componente3 = Matrix LED de 8x8 basada en MAX7219
  Componente4 = Matrix LED de 8x8 basada en MAX7219
  Componente5 = Matrix LED de 8x8 basada en MAX7219
  ZS-042_RTC1 = ZS-042 RTC Module

nets:
  GND: Componente1.GND, Componente2.GND#1, ZS-042_RTC1.GND
  N1: Componente1.D6, Componente2.CLK
  N2: Componente1.D7, Componente2.CS
  N3: Componente1.D8, Componente2.DIN
  VIN: Componente1.VIN, ZS-042_RTC1.VCC
  5V: Componente1.5V, Componente2.VCC
  N4: Componente1.A5, ZS-042_RTC1.SCL
  N5: Componente1.A4, ZS-042_RTC1.SDA
  N6: Componente2.VCC(OUT), Componente3.VCC
  N7: Componente2.GND#6, Componente3.GND#1
  N8: Componente2.CS(OUT), Componente3.CS
  N9: Componente2.CLK(OUT), Componente3.CLK
  N10: Componente2.DOUT, Componente3.DIN
  N11: Componente3.VCC(OUT), Componente4.VCC
  N12: Componente3.GND#6, Componente4.GND#1
  N13: Componente3.CS(OUT), Componente4.CS
  N14: Componente3.CLK(OUT), Componente4.CLK
  N15: Componente3.DOUT, Componente4.DIN
  N16: Componente4.VCC(OUT), Componente5.VCC
  N17: Componente4.GND#6, Componente5.GND
  N18: Componente4.CS(OUT), Componente5.CS
  N19: Componente4.CLK(OUT), Componente5.CLK
  N20: Componente4.DOUT, Componente5.DIN
